# Fritzing sketch Esp32cam (saved by Fritzing 0.9.4)
circuit board: 8.46667cm x 5.64444cm

parts:
  ESP32_-_Back1 = ESP32 - CAM
  part = FTDI Basic Programmer

nets:
  N1: ESP32_-_Back1.5V, part.POWER
  N2: ESP32_-_Back1.GPIO0, ESP32_-_Back1.GND#12
  N3: ESP32_-_Back1.GPIO3_/_RX, part.TXO
  N4: ESP32_-_Back1.GPIO1_/_TX, part.RXI
  N5: ESP32_-_Back1.GND#16, part.GND

notes:
  FT232RL
  USB TO TTL
  Set FTDI interface for 5 volts
  (*) Jumper GPIO 0 to GND for programming
  *

custom parts:
  ESP32 - CAM: The ESP32-CAM has a very competitive small-size camera module that can operate independently as a minimum system with a footprint of only 27*40.5*4.5mm and a deep sleep current of up to 6mA.
